# Fritzing sketch GCAnalogInputCircuit (saved by Fritzing 0.9.2b)
circuit board: 5.27153cm x 5.47553cm
breadboards: 1

parts:
  Part1 = Arduino Uno (Rev3)
  R1 = Resistor [tolerance=±5% resistance=1k package=THT]
  R2 = Resistor [tolerance=±5% resistance=1k package=THT]
  StartSwitch = Pushbutton [package="[THT]"]
  RunningLED = LED - 5mm [color="Green (555nm)" package="5 mm [THT]"]
  R3 = Resistor [tolerance=±5% resistance=470 package=THT]
  U1 = mystery part, 2 pins [chip_label=GC]  # not connected
  StopSwitch = Pushbutton [package="[THT]"]

nets:
  N1: Part1.D8, R1.Pin_1, StartSwitch.Pin_3, StartSwitch.Pin_4
  N2: Part1.GND, R1.Pin_0, R2.Pin_0, R3.Pin_1
  N3: Part1.D2, RunningLED.anode
  N4: Part1.D7, R2.Pin_1, StopSwitch.Pin_3, StopSwitch.Pin_4
  N5: Part1.5V, StartSwitch.Pin_1, StartSwitch.Pin_2, StopSwitch.Pin_1, StopSwitch.Pin_2
  N6: RunningLED.cathode, R3.Pin_0

notes:
  GC
  HP5890
  Serial 1 or 2 output
