# Fritzing sketch GCAnalogInputCircuitADS (saved by Fritzing 0.9.2b)
circuit board: 8.46667cm x 5.64444cm
breadboards: 1

parts:
  ADS1115 = ADS1115 16-bit ADC Breakout
  Schmitt_Inv-Trig = SN74HC14N [package="DIP14 [THT]"]
  C1 = Electrolytic Capacitor [capacitance=10µF voltage=50V package="100 mil [THT, electrolytic]"]
  C2 = Electrolytic Capacitor [capacitance=10µF voltage=50V package="100 mil [THT, electrolytic]"]
  R1 = Resistor [tolerance=±1% resistance=100 package=THT]
  R2 = Resistor [tolerance=±1% resistance=100 package=THT]
  R3 = Resistor [tolerance=±1% resistance=10k package=THT]
  R4 = Resistor [tolerance=±1% resistance=10k package=THT]
  LED1 = LED - 5mm [color="Green (565nm)" package="5 mm [THT]"]
  R6 = Resistor [tolerance=±1% resistance=12k package=THT]
  C3 = Ceramic Capacitor [capacitance=100nF voltage=50V package="100 mil [THT, multilayer]"]
  R5 = Resistor [tolerance=±1% resistance=470 package=THT]
  Part1 = Arduino Uno (Rev3)
  Stop = Pushbutton [package=THT]
  Start = Pushbutton [package=THT]
  C4 = Electrolytic Capacitor [capacitance=10µF voltage=50V package="100 mil [THT, electrolytic]"]
  C5 = Ceramic Capacitor [capacitance=100nF voltage=50V package="100 mil [THT, multilayer]"]
  J1 = female pin header, 4 pins [form="♀ (female)"]

nets:
  VDD: ADS1115.VDD, Schmitt_Inv-Trig.VCC, R3.Pin_0, R4.Pin_0, Part1.5V, C4.-, C5.0
  GND: ADS1115.GND, Schmitt_Inv-Trig.GND, C1.-, C2.-, C3.1, R5.Pin_1, Part1.GND, Stop.leg1, Start.leg1, C4.+, C5.1, J1.pin2, J1.pin3
  N1: ADS1115.SCL, ADS1115.ADDR, Part1.A5/SCL
  N2: ADS1115.SDA, Part1.A4/SDA
  N3: ADS1115.A0, R6.Pin_1, C3.0
  N4: Schmitt_Inv-Trig.1A, C1.+, R1.Pin_1
  N5: Schmitt_Inv-Trig.1Y, Part1.D6_PWM
  N6: Schmitt_Inv-Trig.2A, C2.+, R2.Pin_1
  N7: Schmitt_Inv-Trig.2Y, Part1.D2
  N8: R1.Pin_0, R3.Pin_1, Start.leg0
  N9: R2.Pin_0, R4.Pin_1, Stop.leg0
  N10: LED1.cathode, R5.Pin_0
  N11: LED1.anode, Part1.D4
  N12: R6.Pin_0, J1.pin1

notes:
  Signal input
  from GC
  yellow signal
  black ground
  white sheath gnd

custom parts:
  ADS1115 16-bit ADC Breakout: ADS1015 12-bit I2C ADC+PGA Breakout
  SN74HC14N: Hex Schmitt-Trigger Inverter
