# Fritzing sketch GCAnalogInputCircuitADS2ChanFinal (saved by Fritzing 0.9.2b)
circuit board: 8.46667cm x 5.64444cm
breadboards: 1

parts:
  ADS1115 = ADS1115 16-bit ADC Breakout
  Schmitt_Inv-Trig = SN74HC14N [package="DIP14 [THT]"]
  C1 = Electrolytic Capacitor [capacitance=10µF voltage=50V package="100 mil [THT, electrolytic]"]
  C2 = Electrolytic Capacitor [capacitance=10µF voltage=50V package="100 mil [THT, electrolytic]"]
  R1 = Resistor [tolerance=±1% resistance=100 package=THT]
  R2 = Resistor [tolerance=±1% resistance=100 package=THT]
  R3 = Resistor [tolerance=±1% resistance=10k package=THT]
  R4 = Resistor [tolerance=±1% resistance=10k package=THT]
  LED1 = LED - 5mm [color="Green (565nm)" package="5 mm [THT]"]
  R6 = Resistor [tolerance=±1% resistance=12k package=THT]
  C3 = Ceramic Capacitor [capacitance=100nF voltage=50V package="100 mil [THT, multilayer]"]
  R5 = Resistor [tolerance=±1% resistance=470 package=THT]
  GC_Arduino = Arduino Uno (Rev3)
  Stop_1 = Pushbutton [package=THT]
  Start_1 = Pushbutton [package=THT]
  C4 = Electrolytic Capacitor [capacitance=10µF voltage=50V package="100 mil [THT, electrolytic]"]
  Signal_2 = female pin header, 4 pins [form="♀ (female)"]
  Signal_1 = female pin header, 4 pins [form="♀ (female)"]
  C6 = Ceramic Capacitor [capacitance=100nF voltage=50V package="100 mil [THT, multilayer]"]
  R7 = Resistor [tolerance=±1% resistance=100 package=THT]
  R8 = Resistor [tolerance=±1% resistance=100 package=THT]
  Start_2 = Pushbutton [package=THT]
  Stop_2 = Pushbutton [package=THT]
  R9 = Resistor [tolerance=±1% resistance=10k package=THT]
  R10 = Resistor [tolerance=±1% resistance=10k package=THT]
  C7 = Electrolytic Capacitor [capacitance=10µF voltage=50V package="100 mil [THT, electrolytic]"]
  C8 = Electrolytic Capacitor [capacitance=10µF voltage=50V package="100 mil [THT, electrolytic]"]
  LED2 = LED - 5mm [color="Green (565nm)" package="5 mm [THT]"]
  R11 = Resistor [tolerance=±1% resistance=470 package=THT]
  R12 = Resistor [tolerance=±1% resistance=12k package=THT]
  C5 = Ceramic Capacitor [capacitance=100nF voltage=50V package="100 mil [THT, multilayer]"]

nets:
  VDD: ADS1115.VDD, Schmitt_Inv-Trig.VCC, R3.Pin_0, R4.Pin_0, GC_Arduino.5V, C4.+, R9.Pin_1, R10.Pin_1, C5.0
  GND: ADS1115.GND, ADS1115.A2, ADS1115.A3, Schmitt_Inv-Trig.GND, C1.-, C2.-, C3.1, R5.Pin_1, GC_Arduino.GND, Stop_1.leg1, Start_1.leg1, C4.-, Signal_2.pin2, Signal_2.pin3, Signal_1.pin2, Signal_1.pin3, C6.1, Start_2.leg1, Stop_2.leg1, C7.-, C8.-, R11.Pin_0, C5.1
  N1: ADS1115.SCL, ADS1115.ADDR, GC_Arduino.A5/SCL
  N2: ADS1115.SDA, GC_Arduino.A4/SDA
  N3: ADS1115.A0, R6.Pin_1, C3.0
  N4: ADS1115.A1, C6.0, R12.Pin_1
  N5: Schmitt_Inv-Trig.1A, C1.+, R1.Pin_1
  N6: Schmitt_Inv-Trig.1Y, GC_Arduino.D9_PWM
  N7: Schmitt_Inv-Trig.2A, C2.+, R2.Pin_1
  N8: Schmitt_Inv-Trig.2Y, GC_Arduino.D8
  N9: Schmitt_Inv-Trig.5Y, GC_Arduino.D2
  N10: Schmitt_Inv-Trig.5A, R8.Pin_1, C8.+
  N11: Schmitt_Inv-Trig.6Y, GC_Arduino.D3_PWM
  N12: Schmitt_Inv-Trig.6A, R7.Pin_1, C7.+
  N13: R1.Pin_0, R3.Pin_1, Start_1.leg0
  N14: R2.Pin_0, R4.Pin_1, Stop_1.leg0
  N15: LED1.cathode, R5.Pin_0
  N16: LED1.anode, GC_Arduino.D10_PWM/SS
  N17: R6.Pin_0, Signal_2.pin1
  N18: GC_Arduino.D4, LED2.anode
  N19: Signal_1.pin1, R12.Pin_0
  N20: R7.Pin_0, Start_2.leg0, R9.Pin_0
  N21: R8.Pin_0, Stop_2.leg0, R10.Pin_0
  N22: LED2.cathode, R11.Pin_1

notes:
  Signal input
  from GC
  yellow signal
  black ground
  white sheath gnd

custom parts:
  ADS1115 16-bit ADC Breakout: ADS1015 12-bit I2C ADC+PGA Breakout
  SN74HC14N: Hex Schmitt-Trigger Inverter
